# Fritzing sketch PulseOximeter (saved by Fritzing 0.9.3b)

parts:
  Part1 = Arduino Nano (Rev3.0)
  SparkFun_Particle_Sensor_Breakout_-_MAX1 = SparkFun MAX30105_Breakout [part_number=SEN-14045]
  J1 = Piezo Speaker
  LED1 = smd LED [color="Red (633nm)" package="1206 [SMD]"]
  S1 = Momentary Switch [package=ksa_sealed_tac_switch]
  TFT1 = 1.44" SPI TFT Graphics Display 128x128 [package=THT]

nets:
  GND: Part1.GND, SparkFun_Particle_Sensor_Breakout_-_MAX1.GND, J1.pin1, LED1.anode, TFT1.pin7
  N1: Part1.D2, SparkFun_Particle_Sensor_Breakout_-_MAX1.!INT
  N2: Part1.D3, S1.4
  N3: Part1.D4, LED1.cathode
  N4: Part1.D5, J1.pin2
  N5: Part1.D8, TFT1.pin4
  N6: Part1.D9, TFT1.pin5
  N7: Part1.D10, TFT1.pin6
  N8: Part1.D11/MOSI, TFT1.pin3
  5V: Part1.5V, SparkFun_Particle_Sensor_Breakout_-_MAX1.5V, S1.3, TFT1.pin1, TFT1.pin8
  N9: Part1.A5, SparkFun_Particle_Sensor_Breakout_-_MAX1.SCL
  N10: Part1.A4, SparkFun_Particle_Sensor_Breakout_-_MAX1.SDA
  N11: Part1.D13/SCK, TFT1.pin2

custom parts:
  SparkFun MAX30105_Breakout: Description: The SparkFun MAX30105 Particle Sensor is a flexible, powerful sensor enabling sensing of distance, heart rate, particle detection and even the blinking of an eye. The MAX30105 has been equipped with three LEDs as well as a very sensitive photon detector. The idea is to pulse the different LEDs, then detect what shines back. Based on the reflected signature it’s possible to detect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
  1.44" SPI TFT Graphics Display 128x128: https://robu.in/product/1-44-inch-tft-lcd-color-screen-module-spi-interface-128-x-128-without-touch/
